# Fritzing sketch Schema_electrica_licenta (saved by Fritzing 0.9.3b)

parts:
  Placa_de_dezvoltare = Arduino Uno (Rev3) - ICSP
  Sursa_alimentare = prefix0000 [part_number=S-350-60]
  B1 = Round Pushbutton
  B4 = Round Pushbutton
  B3 = Round Pushbutton
  B2 = Round Pushbutton
  LED1 = smd LED [color="Green (570nm)" package="0603 [SMD]"]
  R1 = Resistor [tolerance=±5% resistance=1k package="0805 [SMD]"]
  R2 = Resistor [tolerance=±5% resistance=1k package="0805 [SMD]"]
  LED2 = smd LED [color="Green (570nm)" package="0603 [SMD]"]
  LED3 = smd LED [color="Green (570nm)" package="0603 [SMD]"]
  LED4 = smd LED [color="Green (570nm)" package="0603 [SMD]"]
  R4 = Resistor [tolerance=±5% resistance=1k package="0805 [SMD]"]
  R3 = Resistor [tolerance=±5% resistance=1k package="0805 [SMD]"]
  Bhalt = Square Pushbutton
  LEDhalt = smd LED [color="Red (635nm)" package="0603 [SMD]"]
  R5 = Resistor [tolerance=±5% resistance=1k package="0805 [SMD]"]
  Limitator = JL012-13-5.2 Lever (Limit) Switch SPDT + NO + NC [part_number=JL012-13-5.2]
  Nema_23 = Stepper Motor - Unipolar
  Driver_motor = DM860A Stepper Motor Driver
  Limitator_tensiune = RioRand LM2596
  R6 = Resistor [tolerance=±5% resistance=1k package="0805 [SMD]"]
  Power_Switch_230_Vac = Pushbutton [package=THT]
  S4 = Pushbutton [package=THT]
  LED_Power = smd LED [color="Green (570nm)" package="0603 [SMD]"]
  LEDrst = smd LED [color="Red (635nm)" package="0603 [SMD]"]
  R7 = Resistor [tolerance=±5% resistance=1k package="0805 [SMD]"]
  BR = Round Pushbutton

nets (from the breadboard view):
  N1: Placa_de_dezvoltare.A0, Limitator.NO
  N2: Placa_de_dezvoltare.A2, Bhalt.leg0
  N3: Placa_de_dezvoltare.A3, BR.leg0
  N4: Placa_de_dezvoltare.GND, B1.leg1, B4.leg1, B3.leg1, B2.leg1, LED1.cathode, LED2.cathode, LED3.cathode, LED4.cathode, Bhalt.leg1, LEDhalt.cathode, Limitator.C, Driver_motor.ENBL-(ENB), Driver_motor.DIR-(DIR), Driver_motor.PUL-(PUL), Limitator_tensiune.Pin_4, R6.Pin_1, LEDrst.cathode, BR.leg1
  N5: Placa_de_dezvoltare.D8, Driver_motor.ENBL+(+5V)
  N6: Placa_de_dezvoltare.D9_PWM, R4.Pin_0
  N7: Placa_de_dezvoltare.D10_PWM/SS, R1.Pin_0
  N8: Placa_de_dezvoltare.D11_PWM/MOSI, R2.Pin_0
  N9: Placa_de_dezvoltare.D12/MISO, R3.Pin_0
  N10: Placa_de_dezvoltare.D13/SCK, R5.Pin_0, R7.Pin_0
  N11: Placa_de_dezvoltare.D2, Driver_motor.PUL+(+5V)
  N12: Placa_de_dezvoltare.D3_PWM, B1.leg0
  N13: Placa_de_dezvoltare.D4, B2.leg0
  N14: Placa_de_dezvoltare.D5_PWM, Driver_motor.DIR+(+5V)
  N15: Placa_de_dezvoltare.D6_PWM, B3.leg0
  N16: Placa_de_dezvoltare.D7, B4.leg0
  N17: Placa_de_dezvoltare.VIN, Limitator_tensiune.Pin_3, LED_Power.anode
  N18: Sursa_alimentare.connector0, Driver_motor.VDC, Limitator_tensiune.Pin_1
  N19: Sursa_alimentare.connector6, Driver_motor.GND, Limitator_tensiune.Pin_2
  N20: Sursa_alimentare.connector7, Power_Switch_230_Vac.leg1
  N21: Sursa_alimentare.connector8, S4.leg1
  N22: LED1.anode, R1.Pin_1
  N23: R2.Pin_1, LED2.anode
  N24: LED3.anode, R3.Pin_1
  N25: LED4.anode, R4.Pin_1
  N26: LEDhalt.anode, R5.Pin_1
  N27: Nema_23.A, Driver_motor.A+
  N28: Nema_23.C, Driver_motor.A-
  N29: Nema_23.B, Driver_motor.B+
  N30: Nema_23.D, Driver_motor.B-
  N31: R6.Pin_0, LED_Power.cathode
  N32: LEDrst.anode, R7.Pin_1

custom parts:
  JL012-13-5.2 Lever (Limit) Switch SPDT + NO + NC: Micro Switch; Model No.: JL012-13.5-2; Actuator Action: Momentary; Actuator Type: Hinge Lever; Contact Configuration: 1NO, 1NC (SPDT) Temperature -25~65℃；Relative humidity: below 85%; Rate Voltage: 125V AC; Rated Current: 1A.
  DM860A Stepper Motor Driver: DM860A is a type of two-phase hybrid stepping motor driver, The drive voltage of which is from 24VDC to 80VDC. It is designed for use with 2-phase hybrid stepper motor of all kinds with 57mm to 110mm outside diameter and less than 8.0A phase current. Mar 2023: Correct pcb layerId as the part won't save correctly in a .fzz file as is.
